// Logisim project Project.circ as structural Verilog: 5 circuits, main circuit main
module main (
  input  CLR_PC,
  input  CLR_Reg,
  output [19:0] out_3
);

  wire alu_1_bne_beq, CLK_out, control_1_alusrc, control_1_jump, control_1_memread, control_1_memwrite,
       control_1_regwrite, Jr;
  wire [1:0] control_1_branch, control_1_memtoreg, control_1_regdst, multiplexer_6_out;
  wire [2:0] multiplexer_2_out;
  wire [3:0] alu_control_1_operation, control_1_aluop;
  wire [19:0] adder_1_out, adder_2_out, alu_1_alu_result, bit_extender_1_out, multiplexer_1_out,
       multiplexer_3_out, multiplexer_4_out, multiplexer_5_out, PC_q, ram_1_data, registers_1_read_data_1,
       registers_1_read_data_2, rom_1_data;

  Register #(.width(20)) PC (.D(multiplexer_1_out), .Q(PC_q), .clk(CLK_out), .clr(CLR_PC));  // open: en
  Multiplexer #(.width(20), .enable("false")) multiplexer_1 (
    .in0(multiplexer_5_out), .in1(registers_1_read_data_1), .out(multiplexer_1_out), .sel(Jr));
  Clock CLK (.out(CLK_out));
  Adder #(.width(20)) adder_1 (.a(20'h1), .b(PC_q), .out(adder_1_out));  // open: cin, cout
  ROM #(.addrWidth(20), .dataWidth(20)) rom_1 (.addr(PC_q), .data(rom_1_data));  // open: sel
  Control control_1 (
    .Jump(control_1_jump), .Branch(control_1_branch), .MemRead(control_1_memread),
    .MemToReg(control_1_memtoreg), .ALUOp(control_1_aluop), .MemWrite(control_1_memwrite),
    .ALUSrc(control_1_alusrc), .RegWrite(control_1_regwrite), .Opcode(rom_1_data[19:16]),
    .RegDst(control_1_regdst));
  Multiplexer #(.select(2), .width(3), .enable("false")) multiplexer_2 (
    .in0(rom_1_data[12:10]), .in1(rom_1_data[9:7]), .in2(3'b111), .out(multiplexer_2_out),
    .sel(control_1_regdst));  // open: in3
  Registers registers_1 (
    .Load(control_1_regwrite), .CLK(CLK_out), .CLR_ALL(CLR_Reg), .Read_Data_1(registers_1_read_data_1),
    .Read_Data_2(registers_1_read_data_2), .Write_Register(multiplexer_2_out), .Write_Data(out_3),
    .Read_Register_1(rom_1_data[15:13]), .Read_Register_2(rom_1_data[12:10]));
  assign bit_extender_1_out = {{10{rom_1_data[9]}}, rom_1_data[9:0]};  // Bit_Extender bit_extender_1
  Multiplexer #(.width(20), .enable("false")) multiplexer_3 (
    .in0(registers_1_read_data_2), .in1(bit_extender_1_out), .out(multiplexer_3_out), .sel(control_1_alusrc));
  Adder #(.width(20)) adder_2 (.a(adder_1_out), .b(bit_extender_1_out), .out(adder_2_out));  // open: cin, cout
  ALU_Control alu_control_1 (.Funct(rom_1_data[3:0]), .ALUop(control_1_aluop), .Operation(alu_control_1_operation));
  Multiplexer #(.width(20), .enable("false")) multiplexer_4 (
    .in0(adder_1_out), .in1(adder_2_out), .out(multiplexer_4_out), .sel(alu_1_bne_beq));
  ALU alu_1 (
    .Data_1(registers_1_read_data_1), .Data_2(multiplexer_3_out), .ALU_Result(alu_1_alu_result),
    .BNE_BEQ(alu_1_bne_beq), .Operation(alu_control_1_operation), .Shamt(rom_1_data[6:4]), .JR_JALR(Jr),
    .Branch(control_1_branch));
  Multiplexer #(.width(20), .enable("false")) multiplexer_5 (
    .in0(multiplexer_4_out), .in1({adder_1_out[19:16], rom_1_data[15:0]}), .out(multiplexer_5_out),
    .sel(control_1_jump));
  Multiplexer #(.width(2), .enable("false")) multiplexer_6 (
    .in0(control_1_memtoreg), .in1(2'b10), .out(multiplexer_6_out), .sel(Jr));
  RAM #(.addrWidth(20), .dataWidth(20), .bus("separate")) ram_1 (
    .addr(alu_1_alu_result), .din(registers_1_read_data_2), .data(ram_1_data), .str(control_1_memwrite),
    .clk(CLK_out), .ld(control_1_memread));  // open: sel, clr
  Multiplexer #(.select(2), .width(20), .enable("false")) multiplexer_7 (
    .in0(alu_1_alu_result), .in1(ram_1_data), .in2(adder_1_out), .out(out_3), .sel(multiplexer_6_out));  // open: in3

  // Notes on the sheet:
  //   Instruction Memory
  //   contents of rom_1 (hex, n*v repeats v):
  //   0 4c80 4c81 4c82 4c83 4c84 4c85 4c86 4c87 4c88 4c89 4c8a 4c8b 163c 164d 620e a00f 17005 26804 37005
  //   46804 56803 66802 76804 86802 90806 a6805 b6803 c6804 d6806 e000c f000d
  //   Data Memory
endmodule

module Control (
  input  [3:0] Opcode,
  output [1:0] RegDst,
  output Jump,
  output [1:0] Branch,
  output MemRead,
  output [1:0] MemToReg,
  output MemWrite,
  output ALUSrc,
  output RegWrite,
  output [3:0] ALUOp
);

  wire decoder_1_out5, decoder_1_out6, decoder_1_out7, decoder_1_out8, decoder_1_out9, decoder_1_out10,
       decoder_1_out11, decoder_1_out12, decoder_1_out13, decoder_1_out14;

  Decoder #(.select(4), .enable("false")) decoder_1 (
    .out0(RegDst[0]), .out1(MemWrite), .out2(MemRead), .out3(Branch[0]), .out4(Branch[1]),
    .out5(decoder_1_out5), .out6(decoder_1_out6), .out7(decoder_1_out7), .out8(decoder_1_out8),
    .out9(decoder_1_out9), .out10(decoder_1_out10), .out11(decoder_1_out11), .out12(decoder_1_out12),
    .out13(decoder_1_out13), .out14(decoder_1_out14), .out15(MemToReg[1]), .sel(Opcode));
  or or_1 (Jump, decoder_1_out14, MemToReg[1]);
  or or_2 (ALUSrc, MemWrite, MemRead, decoder_1_out5, decoder_1_out6, decoder_1_out7, decoder_1_out8, decoder_1_out9, decoder_1_out10, decoder_1_out11, decoder_1_out12, decoder_1_out13);
  or or_3 (RegWrite, MemToReg[1], decoder_1_out13, decoder_1_out12, decoder_1_out11, decoder_1_out10, decoder_1_out9, decoder_1_out8, decoder_1_out7, decoder_1_out6, decoder_1_out5, RegDst[0], MemRead);
  or or_4 (ALUOp[0], RegDst[0], Branch[0], Branch[1], decoder_1_out6, decoder_1_out8, decoder_1_out10, decoder_1_out12);
  or or_5 (ALUOp[1], decoder_1_out7, decoder_1_out8, decoder_1_out11, decoder_1_out12);
  or or_6 (ALUOp[2], decoder_1_out9, decoder_1_out10, decoder_1_out11, decoder_1_out12);
  or or_7 (ALUOp[3], RegDst[0], decoder_1_out13);

  assign MemToReg[0] = MemRead;
  assign RegDst[1] = MemToReg[1];
endmodule

module Registers (
  input  [2:0] Read_Register_1,
  input  [19:0] Write_Data,
  input  Load,
  input  CLK,
  input  CLR_ALL,
  input  [2:0] Write_Register,
  input  [2:0] Read_Register_2,
  output [19:0] Read_Data_1,
  output [19:0] Read_Data_2
);

  wire and_1_out, and_2_out, and_3_out, and_4_out, and_5_out, and_6_out, and_7_out, and_8_out, D00, D01, D02,
       D03, D04, D05, D06, D07;
  wire [19:0] M00, M01, M02, M03, M04, M05, M06, M07;

  Decoder #(.select(3), .enable("false")) decoder_1 (
    .out0(D00), .out1(D01), .out2(D02), .out3(D03), .out4(D04), .out5(D05), .out6(D06), .out7(D07),
    .sel(Write_Register));
  and and_1 (and_1_out, Load, D00);
  and and_2 (and_2_out, Load, D01);
  and and_3 (and_3_out, Load, D02);
  and and_4 (and_4_out, Load, D03);
  Register #(.width(20)) r0 (.D(Write_Data), .en(and_1_out), .Q(M00), .clk(CLK), .clr(CLR_ALL));
  Register #(.width(20)) r1 (.D(Write_Data), .en(and_2_out), .Q(M01), .clk(CLK), .clr(CLR_ALL));
  Register #(.width(20)) r2 (.D(Write_Data), .en(and_3_out), .Q(M02), .clk(CLK), .clr(CLR_ALL));
  Register #(.width(20)) r3 (.D(Write_Data), .en(and_4_out), .Q(M03), .clk(CLK), .clr(CLR_ALL));
  and and_5 (and_5_out, Load, D04);
  and and_6 (and_6_out, Load, D05);
  and and_7 (and_7_out, Load, D06);
  and and_8 (and_8_out, Load, D07);
  Register #(.width(20)) r4 (.D(Write_Data), .en(and_5_out), .Q(M04), .clk(CLK), .clr(CLR_ALL));
  Register #(.width(20)) r5 (.D(Write_Data), .en(and_6_out), .Q(M05), .clk(CLK), .clr(CLR_ALL));
  Register #(.width(20)) r6 (.D(Write_Data), .en(and_7_out), .Q(M06), .clk(CLK), .clr(CLR_ALL));
  Register #(.width(20)) r7 (.D(Write_Data), .en(and_8_out), .Q(M07), .clk(CLK), .clr(CLR_ALL));
  Multiplexer #(.select(3), .width(20), .enable("false")) multiplexer_1 (
    .in0(M00), .in1(M01), .in2(M02), .in3(M03), .in4(M04), .in5(M05), .in6(M06), .in7(M07),
    .out(Read_Data_1), .sel(Read_Register_1));
  Multiplexer #(.select(3), .width(20), .enable("false")) multiplexer_2 (
    .in0(M00), .in1(M01), .in2(M02), .in3(M03), .in4(M04), .in5(M05), .in6(M06), .in7(M07),
    .out(Read_Data_2), .sel(Read_Register_2));

  // Other names for the same wires on the sheet: CLR = CLR_ALL; D[19:0] = Write_Data; LD = Load
endmodule

module ALU (
  input  [3:0] Operation,
  input  [19:0] Data_1,
  input  [19:0] Data_2,
  input  [2:0] Shamt,
  input  [1:0] Branch,
  output JR_JALR,
  output [19:0] ALU_Result,
  output BNE_BEQ
);

  wire and_3_out, and_4_out, comparator_1_lt, nor_2_out;
  wire [4:0] bit_extender_1_out;
  wire [19:0] adder_1_out, and_1_out, bit_extender_2_out, divider_1_out, multiplier_1_out, nand_1_out,
       nor_1_out, not_1_out, or_1_out, shifter_1_out, shifter_2_out, subtractor_1_out, xnor_1_out, xor_1_out;

  assign bit_extender_1_out = {{2{1'b0}}, Shamt};  // Bit_Extender bit_extender_1
  Adder #(.width(20)) adder_1 (.a(Data_1), .b(Data_2), .out(adder_1_out));  // open: cin, cout
  Subtractor #(.width(20)) subtractor_1 (.a(Data_1), .b(Data_2), .out(subtractor_1_out));  // open: bin, bout
  Multiplier #(.width(20)) multiplier_1 (.a(Data_1), .b(Data_2), .out(multiplier_1_out));  // open: cin, cout
  Divider #(.width(20)) divider_1 (.a(Data_1), .b(Data_2), .out(divider_1_out));  // open: upper, rem
  Comparator #(.width(20), .mode("unsigned")) comparator_1 (
    .a(Data_1), .b(Data_2), .lt(comparator_1_lt));  // open: gt, eq
  assign and_1_out = Data_1 & Data_2;  // AND_Gate and_1, 20 bits wide
  assign or_1_out = Data_1 | Data_2;  // OR_Gate or_1, 20 bits wide
  assign not_1_out = ~Data_2;  // NOT_Gate not_1, 20 bits wide
  assign nor_1_out = ~(Data_1 | Data_2);  // NOR_Gate nor_1, 20 bits wide
  assign nand_1_out = ~(Data_1 & Data_2);  // NAND_Gate nand_1, 20 bits wide
  assign xor_1_out = Data_1 ^ Data_2;  // XOR_Gate xor_1, 20 bits wide
  assign xnor_1_out = ~(Data_1 ^ Data_2);  // XNOR_Gate xnor_1, 20 bits wide
  Shifter #(.width(20)) shifter_1 (.in(Data_2), .\dist (bit_extender_1_out), .out(shifter_1_out));
  Shifter #(.width(20), .shift("lr")) shifter_2 (.in(Data_2), .\dist (bit_extender_1_out), .out(shifter_2_out));
  assign bit_extender_2_out = {{19{1'b0}}, comparator_1_lt};  // Bit_Extender bit_extender_2
  Multiplexer #(.select(4), .width(20), .enable("false")) multiplexer_1 (
    .in0(adder_1_out), .in1(subtractor_1_out), .in2(multiplier_1_out), .in3(divider_1_out),
    .in4(bit_extender_2_out), .in5(and_1_out), .in6(or_1_out), .in7(not_1_out), .in8(nor_1_out),
    .in9(nand_1_out), .in10(xor_1_out), .in11(xnor_1_out), .in12(shifter_1_out), .in13(shifter_2_out),
    .out(ALU_Result), .sel(Operation));  // open: in14, in15
  and and_2 (JR_JALR, Operation[1], Operation[2], Operation[3]);
  nor nor_2 (nor_2_out, ALU_Result[0], ALU_Result[1], ALU_Result[2], ALU_Result[3], ALU_Result[4], ALU_Result[5], ALU_Result[6], ALU_Result[7], ALU_Result[8], ALU_Result[9], ALU_Result[10], ALU_Result[11], ALU_Result[12], ALU_Result[13], ALU_Result[14], ALU_Result[15], ALU_Result[16], ALU_Result[17], ALU_Result[18], ALU_Result[19]);
  and and_3 (and_3_out, nor_2_out, Branch[0]);
  or or_2 (BNE_BEQ, and_3_out, and_4_out);
  and and_4 (and_4_out, Branch[1], ~nor_2_out);  // AND_Gate
endmodule

module ALU_Control (
  input  [3:0] Funct,
  input  [3:0] ALUop,
  output [3:0] Operation
);

  wire decoder_1_out1, decoder_1_out2, decoder_1_out3, decoder_1_out4, decoder_1_out5, decoder_1_out6,
       decoder_1_out7, decoder_1_out8, decoder_1_out9, or_1_out, or_2_out, or_3_out, or_4_out;

  Decoder #(.select(4), .enable("false")) decoder_1 (
    .out1(decoder_1_out1), .out2(decoder_1_out2), .out3(decoder_1_out3), .out4(decoder_1_out4),
    .out5(decoder_1_out5), .out6(decoder_1_out6), .out7(decoder_1_out7), .out8(decoder_1_out8),
    .out9(decoder_1_out9), .sel(ALUop));  // open: out0, out10, out11, out12, out13, out14, out15
  or or_1 (or_1_out, decoder_1_out1, decoder_1_out2, decoder_1_out4, decoder_1_out6, decoder_1_out8);
  or or_2 (or_2_out, decoder_1_out3, decoder_1_out4, decoder_1_out8, decoder_1_out7);
  or or_3 (or_3_out, decoder_1_out4, decoder_1_out3, decoder_1_out2);
  or or_4 (or_4_out, decoder_1_out5, decoder_1_out6, decoder_1_out7, decoder_1_out8);
  Multiplexer #(.enable("false")) multiplexer_1 (
    .in0(or_1_out), .in1(Funct[0]), .out(Operation[0]), .sel(decoder_1_out9));
  Multiplexer #(.enable("false")) multiplexer_2 (
    .in0(or_2_out), .in1(Funct[1]), .out(Operation[1]), .sel(decoder_1_out9));
  Multiplexer #(.enable("false")) multiplexer_3 (
    .in0(or_3_out), .in1(Funct[2]), .out(Operation[2]), .sel(decoder_1_out9));
  Multiplexer #(.enable("false")) multiplexer_4 (
    .in0(or_4_out), .in1(Funct[3]), .out(Operation[3]), .sel(decoder_1_out9));
endmodule
